// Logisim project MIPS.circ as structural Verilog: 1 circuit, main circuit main
module main (
);

  wire alu_1_p4, and_1_out, button_1_out, CLK, controlunit_1_p1, controlunit_1_p4, controlunit_1_p5,
       controlunit_1_p6, controlunit_1_p7, controlunit_1_p8, controlunit_1_p9, controlunit_1_p10;
  wire [4:0] multiplexer_3_out;
  wire [7:0] adder_1_out, multiplexer_1_out, multiplexer_2_out, PC_q;
  wire [27:0] bit_extender_3_out, shifter_1_out;
  wire [31:0] adder_2_out, alu_1_p5, bit_extender_1_out, bit_extender_2_out, data_mem_1_rd,
       multiplexer_4_out, multiplexer_5_out, regfile32_1_rd1, regfile32_1_rd2, rom_1_data, shifter_2_out;

  Clock clock_1 (.out(CLK));
  // Probe on adder_1_out
  Multiplexer #(.width(8)) multiplexer_1 (
    .in0(adder_1_out), .in1(adder_2_out[7:0]), .out(multiplexer_1_out), .sel(and_1_out));  // open: en
  Button button_1 (.out(button_1_out));
  // Probe on adder_2_out[7:0]
  Multiplexer #(.width(8)) multiplexer_2 (
    .in0(multiplexer_1_out), .in1(shifter_1_out[7:0]), .out(multiplexer_2_out), .sel(controlunit_1_p1));  // open: en
  Register PC (.D(multiplexer_2_out), .Q(PC_q), .clk(CLK), .clr(button_1_out));  // open: en
  Adder adder_1 (.a(PC_q), .b(8'h4), .out(adder_1_out));  // open: cin, cout
  ROM #(.addrWidth(6), .dataWidth(32)) rom_1 (.addr(PC_q[7:2]), .data(rom_1_data));  // open: sel
  assign bit_extender_1_out = {{24{1'b0}}, adder_1_out};  // Bit_Extender bit_extender_1
  // ControlUnit controlunit_1: pin names not known; wires that end beside it: controlunit_1_p1, rom_1_data[31:26], rom_1_data[5:0], controlunit_1_p4, controlunit_1_p5, controlunit_1_p6, controlunit_1_p7, controlunit_1_p8, controlunit_1_p9, controlunit_1_p10
  assign bit_extender_2_out = {{16{rom_1_data[15]}}, rom_1_data[15:0]};  // Bit_Extender bit_extender_2
  assign bit_extender_3_out = {{2{rom_1_data[25]}}, rom_1_data[25:0]};  // Bit_Extender bit_extender_3
  RegFile32 regfile32_1 (
    .AD1(rom_1_data[25:21]), .AD2(rom_1_data[20:16]), .CLK(CLK), .WE(controlunit_1_p9),
    .AD3(multiplexer_3_out), .WD3(multiplexer_5_out), .RD1(regfile32_1_rd1), .RD2(regfile32_1_rd2));
  Multiplexer #(.width(5)) multiplexer_3 (
    .in0(rom_1_data[20:16]), .in1(rom_1_data[15:11]), .out(multiplexer_3_out), .sel(controlunit_1_p8));  // open: en
  Shifter #(.width(28)) shifter_1 (.in(bit_extender_3_out), .\dist (5'b00010), .out(shifter_1_out));
  Multiplexer #(.width(32)) multiplexer_4 (
    .in0(regfile32_1_rd2), .in1(bit_extender_2_out), .out(multiplexer_4_out), .sel(controlunit_1_p7));  // open: en
  // Probe on bit_extender_2_out
  // ALU alu_1: pin names not known; wires that end beside it: regfile32_1_rd1, multiplexer_4_out, controlunit_1_p10, alu_1_p4, alu_1_p5
  // Probe on shifter_2_out
  // Probe on bit_extender_1_out
  Shifter #(.width(32)) shifter_2 (.in(bit_extender_2_out), .\dist (5'b00010), .out(shifter_2_out));
  and and_1 (and_1_out, controlunit_1_p6, alu_1_p4);
  Adder #(.width(32)) adder_2 (.a(shifter_2_out), .b(bit_extender_1_out), .out(adder_2_out));  // open: cin, cout
  Data_Mem data_mem_1 (.A(alu_1_p5), .CLK(CLK), .WE(controlunit_1_p5), .WD(regfile32_1_rd2), .RD(data_mem_1_rd));
  Multiplexer #(.width(32)) multiplexer_5 (
    .in0(alu_1_p5), .in1(data_mem_1_rd), .out(multiplexer_5_out), .sel(controlunit_1_p4));  // open: en

  // Notes on the sheet:
  //   A AND NOT B : 100
  //   A OR NOT B : 101
  //   AND : 000
  //   OR : 001
  //   + : 010
  //   A - B : 110
  //   SLT : 111
  //   add t2 t1 t0
  //   lw t0 0x00(zero)
  //   lw t1 0x02(zero)
  //   contents of rom_1 (hex, n*v repeats v):
  //   8c080000 21090005
endmodule
